# Fritzing sketch OutputSimulator (saved by Fritzing 0.9.6b)
circuit board: 5.85cm x 1.85cm
breadboards: 1

parts:
  LED1 = LED - 5mm [color="Red (633nm)" current=0.030 package="5 mm [THT]"]
  LED2 = LED - 5mm [color="Red (633nm)" current=0.030 package="5 mm [THT]"]
  LED3 = LED - 5mm [color="Red (633nm)" current=0.030 package="5 mm [THT]"]
  LED4 = LED - 5mm [color="Red (633nm)" current=0.030 package="5 mm [THT]"]
  LED4_2 = LED - 5mm [color="Red (633nm)" current=0.030 package="5 mm [THT]"]
  LED8 = LED - 5mm [color="Red (633nm)" current=0.030 package="5 mm [THT]"]
  LED2_2 = LED - 5mm [color="Red (633nm)" current=0.030 package="5 mm [THT]"]
  LED7 = LED - 5mm [color="Red (633nm)" current=0.030 package="5 mm [THT]"]
  LED11 = LED - 5mm [color="Red (633nm)" current=0.030 package="5 mm [THT]"]
  LED12 = LED - 5mm [color="Red (633nm)" current=0.030 package="5 mm [THT]"]
  LED13 = LED - 5mm [color="Red (633nm)" current=0.030 package="5 mm [THT]"]
  LED3_2 = LED - 5mm [color="Red (633nm)" current=0.030 package="5 mm [THT]"]
  LED15 = LED - 5mm [color="Red (633nm)" current=0.030 package="5 mm [THT]"]
  LED1_2 = LED - 5mm [color="Red (633nm)" current=0.030 package="5 mm [THT]"]
  LED5 = LED - 5mm [color="Red (633nm)" current=0.030 package="5 mm [THT]"]
  LED6 = LED - 5mm [color="Red (633nm)" current=0.030 package="5 mm [THT]"]
  J5 = male pin header, 2 pins [form="♂ (male)"]
  J1 = male pin header, 4 pins [form="♂ (male)"]
  J2 = male pin header, 4 pins [form="♂ (male)"]
  J3 = male pin header, 4 pins [form="♂ (male)"]
  J4 = male pin header, 4 pins [form="♂ (male)"]

nets:
  GND: LED1.cathode, LED2.cathode, LED3.cathode, LED4.cathode, LED11.cathode, LED12.cathode, LED13.cathode, LED15.cathode, J5.pin2
  N1: LED1.anode, J3.pin1
  N2: LED2.anode, J3.pin3
  N3: LED3.anode, J4.pin1
  N4: LED4.anode, J4.pin3
  N5: LED4_2.cathode, J1.pin4
  V+: LED4_2.anode, LED8.anode, LED2_2.anode, LED7.anode, LED3_2.anode, LED1_2.anode, LED5.anode, LED6.anode, J5.pin1
  N6: LED8.cathode, J2.pin4
  N7: LED2_2.cathode, J1.pin2
  N8: LED7.cathode, J2.pin3
  N9: LED11.anode, J3.pin2
  N10: LED12.anode, J4.pin2
  N11: LED13.anode, J3.pin4
  N12: LED3_2.cathode, J1.pin3
  N13: LED15.anode, J4.pin4
  N14: LED1_2.cathode, J1.pin1
  N15: LED5.cathode, J2.pin1
  N16: LED6.cathode, J2.pin2

notes:
  V+
  V-
